// Logisim project contador4bits.circ as structural Verilog: 3 circuits, main circuit main
module main (
  input  Enable,
  input  Clear,
  output q3,
  output q2,
  output q1,
  output q0
);

  wire CLOCK_out;
  wire [3:0] Incrementador_s0;

  Clock CLOCK (.out(CLOCK_out));
  Register #(.width(4), .Select("low")) register_1 (
    .D(Incrementador_s0), .en(Enable), .Q({q3, q2, q1, q0}), .clk(CLOCK_out), .clr(Clear), .cs(1'b0),
    .preset(1'b0));
  Incrementador Incrementador (
    .s0(Incrementador_s0[0]), .s1(Incrementador_s0[1]), .s2(Incrementador_s0[2]), .s3(Incrementador_s0[3]),
    .a0(q0), .a1(q1), .a2(q2), .a3(q3));  // open: c0
endmodule

module Meio_Somador (
  input  a,
  input  b,
  output s,
  output c0
);

  xor xor_1 (s, a, b);
  and and_1 (c0, a, b);
endmodule

module Incrementador (
  input  a0,
  input  a1,
  input  a2,
  input  a3,
  output s0,
  output s1,
  output s2,
  output s3,
  output c0
);

  wire meio_somador_1_c0, meio_somador_2_c0, meio_somador_3_c0;

  Meio_Somador meio_somador_1 (.a(1'b1), .b(a0), .s(s0), .c0(meio_somador_1_c0));
  Meio_Somador meio_somador_2 (.a(meio_somador_3_c0), .b(a2), .s(s2), .c0(meio_somador_2_c0));
  Meio_Somador meio_somador_3 (.a(meio_somador_1_c0), .b(a1), .s(s1), .c0(meio_somador_3_c0));
  Meio_Somador meio_somador_4 (.a(meio_somador_2_c0), .b(a3), .s(s3), .c0(c0));
endmodule
